# Fritzing sketch MyNewProject (saved by Fritzing 0.9.3b)

parts:
  元件1 = Rotoshield - Motor driver shield for Arduino
  元件2 = Arduino Uno (Rev3)
  M1 = DC Motor
  M2 = DC Motor  # not connected
  J1 = Basic Servo  # not connected
  M3 = Stepper Motor - Bipolar
  元件3 = Bluetooth Module Breakout - Roving Networks (RN-41)
  VCC1 = Battery  # not connected

nets:
  N1: 元件1.DIG_3, 元件2.D3_PWM
  N2: 元件1.DIG_4, 元件2.D4
  N3: 元件1.DIG_5, 元件2.D5_PWM
  N4: 元件1.DIG_6, 元件2.D6_PWM
  N5: 元件1.DIG_7, 元件2.D7
  N6: 元件1.DIG_8, 元件2.D8
  N7: 元件1.DIG_11, 元件2.D11_PWM/MOSI
  N8: 元件1.DIG_12, 元件2.D12/MISO
  +5V: 元件1.+5V, 元件2.5V
  GND: 元件1.GND, 元件2.GND, 元件3.GND
  N9: 元件1.M1-2, M3.C
  N10: 元件1.M1-1, M3.A
  N11: 元件1.M2-2, M3.D
  N12: 元件1.M2-1, M3.B
  N13: 元件1.M4-1, M1.pin_1
  N14: 元件2.D0/RX, 元件3.UARTTX
  N15: 元件2.D1/TX, 元件3.UARTRX
  3V3: 元件2.3V3, 元件3.VCC

notes:
  L293D
  适配：Mega,Uno
  只适用于6V以上的电机
